// Logisim project Processor_Architecture.circ as structural Verilog: 13 circuits, main circuit main
module main (
  input  [15:0] Data,
  input  [5:0] Address,
  input  Store
);

  wire clk, clr;
  wire [3:0] joystick_1_x, joystick_1_y;
  wire [4:0] adapter_1_out_7, memoryconverter_1_address_output;
  wire [11:0] ROMAddress;
  wire [15:0] ROMData;
  wire [31:0] adapter_1_data_output, demultiplexer_1_out0, demultiplexer_1_out1, demultiplexer_1_out2,
       demultiplexer_1_out3, demultiplexer_1_out4, demultiplexer_1_out5, demultiplexer_1_out6,
       demultiplexer_1_out7, demultiplexer_1_out8, demultiplexer_1_out9, demultiplexer_1_out10,
       demultiplexer_1_out11, demultiplexer_1_out12, demultiplexer_1_out13, demultiplexer_1_out14,
       demultiplexer_1_out15, demultiplexer_1_out16, demultiplexer_1_out17, demultiplexer_1_out18,
       demultiplexer_1_out19, demultiplexer_1_out20, demultiplexer_1_out21, demultiplexer_1_out22,
       demultiplexer_1_out23, demultiplexer_1_out24, demultiplexer_1_out25, demultiplexer_1_out26,
       demultiplexer_1_out27, demultiplexer_1_out28, demultiplexer_1_out29, demultiplexer_1_out30,
       demultiplexer_1_out31, memoryconverter_1_data_output;

  Clock Clock (.out(clk));
  Button Clear (.out(clr));
  Joystick joystick_1 (.x(joystick_1_x), .y(joystick_1_y));
  ControllerAdapter controlleradapter_1 (.X_Axis(joystick_1_x), .Y_Axis(joystick_1_y), .Clock(Store));  // open: out_4
  ROM #(.addrWidth(12), .dataWidth(16)) rom_1 (.addr(ROMAddress), .data(ROMData));  // open: sel
  RAM #(.addrWidth(16), .dataWidth(16), .bus("separate")) ram_1 (
    .clk(clk), .clr(clr));  // open: addr, din, data, str, sel, ld
  Precessor precessor_1 (.in_1(ROMData), .Clock(clk), .Reset(clr), .NextAddress(ROMAddress));
  DotMatrix #(.matrixcols(32), .matrixrows(32), .persist(64)) dotmatrix_1 (
    .col0(demultiplexer_1_out0), .col1(demultiplexer_1_out1), .col2(demultiplexer_1_out2),
    .col3(demultiplexer_1_out3), .col4(demultiplexer_1_out4), .col5(demultiplexer_1_out5),
    .col6(demultiplexer_1_out6), .col7(demultiplexer_1_out7), .col8(demultiplexer_1_out8),
    .col9(demultiplexer_1_out9), .col10(demultiplexer_1_out10), .col11(demultiplexer_1_out11),
    .col12(demultiplexer_1_out12), .col13(demultiplexer_1_out13), .col14(demultiplexer_1_out14),
    .col15(demultiplexer_1_out15), .col16(demultiplexer_1_out16), .col17(demultiplexer_1_out17),
    .col18(demultiplexer_1_out18), .col19(demultiplexer_1_out19), .col20(demultiplexer_1_out20),
    .col21(demultiplexer_1_out21), .col22(demultiplexer_1_out22), .col23(demultiplexer_1_out23),
    .col24(demultiplexer_1_out24), .col25(demultiplexer_1_out25), .col26(demultiplexer_1_out26),
    .col27(demultiplexer_1_out27), .col28(demultiplexer_1_out28), .col29(demultiplexer_1_out29),
    .col30(demultiplexer_1_out30), .col31(demultiplexer_1_out31));
  MemoryConverter memoryconverter_1 (
    .Address_Input(Address), .Data_Input(Data), .Store(Store), .Clock(clk), .Clear(clr),
    .Data_Output(memoryconverter_1_data_output), .Address_Output(memoryconverter_1_address_output));  // open: OutStore
  Demultiplexer #(.select(5), .width(32)) demultiplexer_1 (
    .out0(demultiplexer_1_out0), .out1(demultiplexer_1_out1), .out2(demultiplexer_1_out2),
    .out3(demultiplexer_1_out3), .out4(demultiplexer_1_out4), .out5(demultiplexer_1_out5),
    .out6(demultiplexer_1_out6), .out7(demultiplexer_1_out7), .out8(demultiplexer_1_out8),
    .out9(demultiplexer_1_out9), .out10(demultiplexer_1_out10), .out11(demultiplexer_1_out11),
    .out12(demultiplexer_1_out12), .out13(demultiplexer_1_out13), .out14(demultiplexer_1_out14),
    .out15(demultiplexer_1_out15), .out16(demultiplexer_1_out16), .out17(demultiplexer_1_out17),
    .out18(demultiplexer_1_out18), .out19(demultiplexer_1_out19), .out20(demultiplexer_1_out20),
    .out21(demultiplexer_1_out21), .out22(demultiplexer_1_out22), .out23(demultiplexer_1_out23),
    .out24(demultiplexer_1_out24), .out25(demultiplexer_1_out25), .out26(demultiplexer_1_out26),
    .out27(demultiplexer_1_out27), .out28(demultiplexer_1_out28), .out29(demultiplexer_1_out29),
    .out30(demultiplexer_1_out30), .out31(demultiplexer_1_out31), .in(adapter_1_data_output),
    .sel(adapter_1_out_7));  // open: en
  Adapter adapter_1 (
    .Address(memoryconverter_1_address_output), .Data_Input(memoryconverter_1_data_output), .Store(Store),
    .Clock(clk), .Clear(clr), .Data_Output(adapter_1_data_output), .out_7(adapter_1_out_7));

  // Other names for the same wires on the sheet: Address_Input[5:0] = Address; Data_Input[15:0] = Data; str = Store

  // Notes on the sheet:
  //   contents of rom_1 (hex, n*v repeats v):
  //   f700 1000
endmodule

module HalfSum (
  input  A,
  input  B,
  output Sum,
  output CarryOut
);

  and and_1 (CarryOut, A, B);
  xor xor_1 (Sum, B, A);
endmodule

module FullSum (
  input  A,
  input  B,
  input  CarryIn,
  output Sum,
  output CarryOut
);

  wire halfsum_1_carryout, halfsum_1_sum, halfsum_2_carryout;

  HalfSum halfsum_1 (.A(A), .B(B), .Sum(halfsum_1_sum), .CarryOut(halfsum_1_carryout));
  HalfSum halfsum_2 (.A(halfsum_1_sum), .B(CarryIn), .Sum(Sum), .CarryOut(halfsum_2_carryout));
  or or_1 (CarryOut, halfsum_2_carryout, halfsum_1_carryout);
endmodule

module Sum (
  input  [15:0] A,
  input  [15:0] B,
  input  CarryIn,
  output CarryOut,
  output [15:0] Sum
);

  wire fullsum_1_carryout, fullsum_2_carryout, fullsum_3_carryout, fullsum_4_carryout, fullsum_5_carryout,
       fullsum_7_carryout, fullsum_8_carryout, fullsum_9_carryout, fullsum_10_carryout, fullsum_11_carryout,
       fullsum_12_carryout, fullsum_13_carryout, fullsum_14_carryout, fullsum_15_carryout,
       fullsum_16_carryout;

  FullSum fullsum_1 (.A(fullsum_14_carryout), .B(B[10]), .CarryIn(A[10]), .Sum(Sum[10]), .CarryOut(fullsum_1_carryout));
  FullSum fullsum_2 (.A(fullsum_1_carryout), .B(B[11]), .CarryIn(A[11]), .Sum(Sum[11]), .CarryOut(fullsum_2_carryout));
  FullSum fullsum_3 (.A(fullsum_2_carryout), .B(B[12]), .CarryIn(A[12]), .Sum(Sum[12]), .CarryOut(fullsum_3_carryout));
  FullSum fullsum_4 (.A(fullsum_3_carryout), .B(B[13]), .CarryIn(A[13]), .Sum(Sum[13]), .CarryOut(fullsum_4_carryout));
  FullSum fullsum_5 (.A(fullsum_4_carryout), .B(B[14]), .CarryIn(A[14]), .Sum(Sum[14]), .CarryOut(fullsum_5_carryout));
  FullSum fullsum_6 (.A(fullsum_5_carryout), .B(B[15]), .CarryIn(A[15]), .Sum(Sum[15]), .CarryOut(CarryOut));
  FullSum fullsum_7 (.A(fullsum_16_carryout), .B(B[2]), .CarryIn(A[2]), .Sum(Sum[2]), .CarryOut(fullsum_7_carryout));
  FullSum fullsum_8 (.A(fullsum_7_carryout), .B(B[3]), .CarryIn(A[3]), .Sum(Sum[3]), .CarryOut(fullsum_8_carryout));
  FullSum fullsum_9 (.A(fullsum_8_carryout), .B(B[4]), .CarryIn(A[4]), .Sum(Sum[4]), .CarryOut(fullsum_9_carryout));
  FullSum fullsum_10 (.A(fullsum_9_carryout), .B(B[5]), .CarryIn(A[5]), .Sum(Sum[5]), .CarryOut(fullsum_10_carryout));
  FullSum fullsum_11 (.A(fullsum_10_carryout), .B(B[6]), .CarryIn(A[6]), .Sum(Sum[6]), .CarryOut(fullsum_11_carryout));
  FullSum fullsum_12 (.A(fullsum_11_carryout), .B(B[7]), .CarryIn(A[7]), .Sum(Sum[7]), .CarryOut(fullsum_12_carryout));
  FullSum fullsum_13 (.A(fullsum_12_carryout), .B(B[8]), .CarryIn(A[8]), .Sum(Sum[8]), .CarryOut(fullsum_13_carryout));
  FullSum fullsum_14 (.A(fullsum_13_carryout), .B(B[9]), .CarryIn(A[9]), .Sum(Sum[9]), .CarryOut(fullsum_14_carryout));
  FullSum fullsum_15 (.A(CarryIn), .B(B[0]), .CarryIn(A[0]), .Sum(Sum[0]), .CarryOut(fullsum_15_carryout));
  FullSum fullsum_16 (.A(fullsum_15_carryout), .B(B[1]), .CarryIn(A[1]), .Sum(Sum[1]), .CarryOut(fullsum_16_carryout));
endmodule

module ULA (
  input  [15:0] A,
  input  [15:0] B,
  input  [3:0] Op,
  output [15:0] Result,
  output Overflow,
  output IsBigger,
  output IsLower
);

  wire Carry_Adder, Carry_Decrement, Carry_Divider, Carry_Increment, Carry_Multiplier, Carry_Subtractor;
  wire [15:0] divider_1_rem, multiplier_1_cout, Output_Adder, Output_AND, Output_Decrement, Output_Divider,
       Output_Increment, Output_Multiplier, Output_NAND, Output_Negator, Output_NOR, Output_Not, Output_OR,
       Output_Shifter_Left, Output_Shifter_Right, Output_Subtractor, Output_XNOR, Output_XOR;

  Adder #(.width(16)) adder_1 (.a(A), .b(B), .out(Output_Adder), .cout(Carry_Adder));  // open: cin
  Subtractor #(.width(16)) subtractor_1 (.a(A), .b(B), .out(Output_Subtractor), .bout(Carry_Subtractor));  // open: bin
  assign Output_AND = A & B;  // AND_Gate and_1, 16 bits wide
  Shifter #(.width(16)) shifter_1 (.in(A), .\dist (B[3:0]), .out(Output_Shifter_Left));
  assign Output_NAND = ~(A & B);  // NAND_Gate nand_1, 16 bits wide
  assign Output_Not = ~A;  // NOT_Gate not_1, 16 bits wide
  assign Output_XNOR = ~(A ^ B);  // XNOR_Gate xnor_1, 16 bits wide
  Adder #(.width(16)) adder_2 (.a(A), .b(16'h1), .out(Output_Increment), .cout(Carry_Increment));  // open: cin
  Multiplier #(.width(16)) multiplier_1 (.a(A), .b(B), .out(Output_Multiplier), .cout(multiplier_1_cout));  // open: cin
  assign Output_OR = A | B;  // OR_Gate or_1, 16 bits wide
  Shifter #(.width(16), .shift("lr")) shifter_2 (.in(A), .\dist (B[3:0]), .out(Output_Shifter_Right));
  assign Output_NOR = ~(A | B);  // NOR_Gate nor_1, 16 bits wide
  Negator #(.width(16)) negator_1 (.in(A), .out(Output_Negator));
  assign Output_XOR = A ^ B;  // XOR_Gate xor_1, 16 bits wide
  Subtractor #(.width(16)) subtractor_2 (
    .a(A), .b(16'h1), .out(Output_Decrement), .bout(Carry_Decrement));  // open: bin
  or or_2 (Carry_Multiplier, multiplier_1_cout[0], multiplier_1_cout[1], multiplier_1_cout[2], multiplier_1_cout[3], multiplier_1_cout[4], multiplier_1_cout[5], multiplier_1_cout[6], multiplier_1_cout[7], multiplier_1_cout[8], multiplier_1_cout[9], multiplier_1_cout[10], multiplier_1_cout[11], multiplier_1_cout[12], multiplier_1_cout[13], multiplier_1_cout[14], multiplier_1_cout[15]);
  Divider #(.width(16)) divider_1 (.a(A), .b(B), .out(Output_Divider), .rem(divider_1_rem));  // open: upper
  or or_3 (Carry_Divider, divider_1_rem[0], divider_1_rem[1], divider_1_rem[2], divider_1_rem[3], divider_1_rem[4], divider_1_rem[5], divider_1_rem[6], divider_1_rem[7], divider_1_rem[8], divider_1_rem[9], divider_1_rem[10], divider_1_rem[11], divider_1_rem[12], divider_1_rem[13], divider_1_rem[14], divider_1_rem[15]);
  Multiplexer #(.select(4), .width(16)) multiplexer_1 (
    .in0(Output_AND), .in1(Output_Subtractor), .in2(Output_Multiplier), .in3(Output_Divider),
    .in4(Output_NAND), .in5(Output_Shifter_Right), .in6(Output_XNOR), .in7(Output_Increment),
    .in8(Output_Decrement), .in9(Output_XOR), .in10(Output_Not), .in11(Output_NOR),
    .in12(Output_Shifter_Left), .in13(Output_Adder), .in14(Output_Negator), .in15(Output_OR), .out(Result),
    .sel(Op));  // open: en
  Multiplexer #(.select(4)) multiplexer_2 (
    .in1(Carry_Subtractor), .in2(Carry_Multiplier), .in3(Carry_Divider), .in7(Carry_Increment),
    .in8(Carry_Decrement), .in13(Carry_Adder), .out(Overflow), .sel(Op));  // open: in0, in4, in5, in6, in9, in10, in11, in12, in14, in15, en
  Comparator #(.width(16)) comparator_1 (.a(A), .b(B), .gt(IsBigger), .lt(IsLower));  // open: eq
endmodule

module LatchSR (
  input  Set,
  input  Reset,
  output Output
);

  wire nand_2_out;

  nand nand_1 (Output, Set, nand_2_out);
  nand nand_2 (nand_2_out, Output, Reset);
endmodule

module LatchD (
  input  Data,
  input  Enable,
  output Output
);

  wire nand_1_out, nand_2_out, not_1_out;

  nand nand_1 (nand_1_out, Data, Enable);
  nand nand_2 (nand_2_out, Enable, not_1_out);
  not not_1 (not_1_out, Data);
  LatchSR latchsr_1 (.Set(nand_1_out), .Reset(nand_2_out), .Output(Output));
endmodule

module FlipFlop (
  input  Data,
  input  Enable,
  input  Clock,
  output out_4
);

  wire and_1_out, latchd_1_output, not_1_out;

  LatchD latchd_1 (.Data(Data), .Enable(and_1_out), .Output(latchd_1_output));
  and and_1 (and_1_out, Enable, Clock);
  not not_1 (not_1_out, Clock);
  LatchD latchd_2 (.Data(latchd_1_output), .Enable(not_1_out), .Output(out_4));
endmodule

module Bank_of_Registrars (
  input  [15:0] Data,
  input  [3:0] Address_A,
  input  Clock,
  input  Reset,
  input  Enable,
  input  [3:0] Address_B,
  output [15:0] Data_A,
  output [15:0] Data_B
);

  wire en0, en1, en2, en3, en4, en5, en6, en7, en8, en9, en10, en11, en12, en13, en14, en15;
  wire [15:0] out0, out1, out2, out3, out4, out5, out6, out7, out8, out9, out10, out11, out12, out13, out14,
       out15;

  Register #(.width(16)) register_1 (.D(Data), .en(en0), .Q(out0), .clk(Clock), .clr(Reset));
  Register #(.width(16)) register_2 (.D(Data), .en(en2), .Q(out2), .clk(Clock), .clr(Reset));
  Register #(.width(16)) register_3 (.D(Data), .en(en4), .Q(out4), .clk(Clock), .clr(Reset));
  Register #(.width(16)) register_4 (.D(Data), .en(en6), .Q(out6), .clk(Clock), .clr(Reset));
  Register #(.width(16)) register_5 (.D(Data), .en(en8), .Q(out8), .clk(Clock), .clr(Reset));
  Register #(.width(16)) register_6 (.D(Data), .en(en10), .Q(out10), .clk(Clock), .clr(Reset));
  Register #(.width(16)) register_7 (.D(Data), .en(en12), .Q(out12), .clk(Clock), .clr(Reset));
  Register #(.width(16)) register_8 (.D(Data), .en(en14), .Q(out14), .clk(Clock), .clr(Reset));
  Register #(.width(16)) register_9 (.D(Data), .en(en1), .Q(out1), .clk(Clock), .clr(Reset));
  Register #(.width(16)) register_10 (.D(Data), .en(en3), .Q(out3), .clk(Clock), .clr(Reset));
  Register #(.width(16)) register_11 (.D(Data), .en(en5), .Q(out5), .clk(Clock), .clr(Reset));
  Register #(.width(16)) register_12 (.D(Data), .en(en7), .Q(out7), .clk(Clock), .clr(Reset));
  Register #(.width(16)) register_13 (.D(Data), .en(en9), .Q(out9), .clk(Clock), .clr(Reset));
  Register #(.width(16)) register_14 (.D(Data), .en(en11), .Q(out11), .clk(Clock), .clr(Reset));
  Register #(.width(16)) register_15 (.D(Data), .en(en13), .Q(out13), .clk(Clock), .clr(Reset));
  Register #(.width(16)) register_16 (.D(Data), .en(en15), .Q(out15), .clk(Clock), .clr(Reset));
  Demultiplexer #(.select(4)) demultiplexer_1 (
    .out0(en0), .out1(en1), .out2(en2), .out3(en3), .out4(en4), .out5(en5), .out6(en6), .out7(en7),
    .out8(en8), .out9(en9), .out10(en10), .out11(en11), .out12(en12), .out13(en13), .out14(en14),
    .out15(en15), .in(Enable), .sel(Address_A));  // open: en
  Multiplexer #(.select(4), .width(16)) multiplexer_1 (
    .in0(out0), .in1(out1), .in2(out2), .in3(out3), .in4(out4), .in5(out5), .in6(out6), .in7(out7),
    .in8(out8), .in9(out9), .in10(out10), .in11(out11), .in12(out12), .in13(out13), .in14(out14),
    .in15(out15), .out(Data_A), .sel(Address_A));  // open: en
  Multiplexer #(.select(4), .width(16)) multiplexer_2 (
    .in0(out0), .in1(out1), .in2(out2), .in3(out3), .in4(out4), .in5(out5), .in6(out6), .in7(out7),
    .in8(out8), .in9(out9), .in10(out10), .in11(out11), .in12(out12), .in13(out13), .in14(out14),
    .in15(out15), .out(Data_B), .sel(Address_B));  // open: en

  // Other names for the same wires on the sheet: clk = Clock; rst = Reset
endmodule

module Precessor (
  input  [15:0] in_1,
  input  Clock,
  input  Reset,
  output [11:0] NextAddress
);

  wire and_5_out, and_10_out, and_11_out, and_16_out, and_17_out, Bigger_Output, Equal, isCmp, isCmpI,
       isCmpOp, isJe, isJg, isJge, isJne, isJump, isJz, isMem, isMov, isMovConst, isOp, JumpCondition,
       Lower_Output, not_1_out, not_2_out, not_3_out, not_4_out, not_5_out, not_6_out, not_7_out, not_8_out,
       not_9_out, not_10_out, not_11_out, not_12_out, not_13_out, not_14_out, not_15_out, not_16_out,
       not_17_out, not_18_out, not_19_out, not_20_out, not_21_out, not_22_out, not_23_out, not_24_out,
       not_25_out, or_1_out, or_3_out, regen, ula_1_isbigger, ula_1_islower;
  wire [3:0] A;
  wire [11:0] adder_1_out, next, nextStack, stack;
  wire [15:0] B, bank_of_registrars_1_data_a, Data, Mem, ULA_Input, ULA_Output;

  not not_1 (not_1_out, in_1[12]);
  not not_2 (not_2_out, in_1[13]);
  not not_3 (not_3_out, in_1[14]);
  not not_4 (not_4_out, in_1[12]);
  not not_5 (not_5_out, in_1[14]);
  not not_6 (not_6_out, in_1[15]);
  not not_7 (not_7_out, in_1[13]);
  not not_8 (not_8_out, in_1[15]);
  and and_1 (isOp, in_1[12], in_1[13], in_1[14], in_1[15]);
  and and_2 (isMovConst, not_1_out, not_2_out, not_3_out, in_1[15]);
  and and_3 (isJe, not_4_out, in_1[13], not_5_out, not_6_out);
  and and_4 (isJge, in_1[12], not_7_out, in_1[14], not_8_out);
  Adder #(.width(12)) adder_1 (.a(NextAddress), .b(12'h1), .out(adder_1_out));  // open: cin, cout
  and and_5 (and_5_out, Equal, isJe);
  or or_1 (or_1_out, Bigger_Output, Lower_Output);
  // Probe on bank_of_registrars_1_data_a
  Bank_of_Registrars bank_of_registrars_1 (
    .Data(Data), .Clock(Clock), .Reset(Reset), .Enable(regen), .Data_A(bank_of_registrars_1_data_a),
    .Data_B(B), .Address_A(A), .Address_B(in_1[3:0]));
  // Probe on B
  not not_9 (not_9_out, in_1[13]);
  not not_10 (not_10_out, in_1[14]);
  and and_6 (isMov, in_1[12], not_9_out, not_10_out, in_1[15]);
  not not_11 (not_11_out, in_1[13]);
  not not_12 (not_12_out, in_1[14]);
  and and_7 (isJump, in_1[12], not_11_out, not_12_out, not_13_out);
  not not_13 (not_13_out, in_1[15]);
  and and_8 (isJne, in_1[12], in_1[13], not_14_out, not_15_out);
  not not_14 (not_14_out, in_1[14]);
  not not_15 (not_15_out, in_1[15]);
  not not_16 (not_16_out, in_1[12]);
  and and_9 (isJz, not_16_out, in_1[13], in_1[14], not_17_out);
  not not_17 (not_17_out, in_1[15]);
  Multiplexer #(.width(12)) multiplexer_1 (
    .in0(adder_1_out), .in1(in_1[11:0]), .out(next), .sel(JumpCondition));  // open: en
  and and_10 (and_10_out, or_1_out, isJne);
  or or_2 (JumpCondition, isJump, and_5_out, and_10_out, and_11_out, and_16_out, and_17_out);
  and and_11 (and_11_out, isJg, Bigger_Output);
  not not_18 (not_18_out, in_1[12]);
  not not_19 (not_19_out, in_1[13]);
  not not_20 (not_20_out, in_1[12]);
  not not_21 (not_21_out, in_1[12]);
  not not_22 (not_22_out, in_1[13]);
  not not_23 (not_23_out, in_1[15]);
  and and_12 (Equal, not_24_out, not_25_out);
  not not_24 (not_24_out, Bigger_Output);
  // Probe on ULA_Output
  ULA ula_1 (
    .A(bank_of_registrars_1_data_a), .B(ULA_Input), .Op(in_1[11:8]), .Result(ULA_Output),
    .IsBigger(ula_1_isbigger), .IsLower(ula_1_islower));  // open: Overflow
  Register #(.width(1)) register_1 (.D(ula_1_islower), .en(isCmpOp), .Q(Lower_Output), .clk(Clock), .clr(Reset));
  and and_13 (isCmp, not_18_out, not_19_out, in_1[14], in_1[15]);
  and and_14 (isCmpI, not_20_out, in_1[13], in_1[14], in_1[15]);
  and and_15 (isJg, not_21_out, not_22_out, in_1[14], not_23_out);
  not not_25 (not_25_out, Lower_Output);
  and and_16 (and_16_out, isJge, or_3_out);
  or or_3 (or_3_out, Bigger_Output, Equal);
  and and_17 (and_17_out, Equal, isJz);
  Register #(.width(12)) u_Stack (.D(nextStack), .Q(stack), .clk(Clock), .clr(Reset));  // open: en
  Register #(.width(1)) register_2 (.D(ula_1_isbigger), .en(isCmpOp), .Q(Bigger_Output), .clk(Clock), .clr(Reset));
  Multiplexer #(.select(2), .width(16)) multiplexer_2 (
    .in0(B), .in1({16{1'b0}}), .in2({{8{1'b0}}, in_1[7:0]}), .out(ULA_Input), .sel({isCmpI, isJz}));  // open: in3, en
  Multiplexer #(.width(4)) multiplexer_3 (.in0(in_1[7:4]), .in1(in_1[11:8]), .out(A), .sel(isMovConst));  // open: en
  Register #(.width(12)) PC (.D(next), .Q(NextAddress), .clk(Clock), .clr(Reset));  // open: en
  Multiplexer #(.select(3), .width(16)) multiplexer_4 (
    .in0(ULA_Output), .in1(Mem), .in2(B), .in4({{8{1'b0}}, in_1[7:0]}), .out(Data),
    .sel({isMovConst, isMov, isMem}));  // open: in3, in5, in6, in7, en
  or or_4 (isCmpOp, isCmp, isCmpI);
  or or_5 (regen, isOp, isMov, isMovConst);

  // Other names for the same wires on the sheet: clk = Clock; crr[11:0] = NextAddress; inst[15:0] = in_1;
  //   s3[3:0] = in_1[15:12]; C[7:0] = in_1[7:0]; L[11:0] = in_1[11:0]; s0[3:0] = in_1[3:0]; s1[3:0] = in_1[7:4];
  //   s2[3:0] = in_1[11:8]; rst = Reset
endmodule

module Adapter (
  input  [4:0] Address,
  input  [31:0] Data_Input,
  input  Store,
  input  Clock,
  input  Clear,
  output [31:0] Data_Output,
  output [4:0] out_7
);

  wire not_1_out, t_ff_1_q, t_ff_2_q, t_ff_3_q, t_ff_4_q;
  wire [4:0] multiplexer_1_out, t_ff_1_qn;
  wire [31:0] ram_1_data, ram_2_data;

  Multiplexer #(.width(5)) multiplexer_1 (
    .in0(Address), .in1(out_7), .out(multiplexer_1_out), .sel(Store));  // open: en
  RAM #(.addrWidth(5), .dataWidth(32), .bus("separate")) ram_1 (
    .addr(multiplexer_1_out), .din(Data_Input), .data(ram_1_data), .str(Store), .clk(Clock), .clr(Clear));  // open: sel, ld
  T_Flip_Flop t_ff_1 (.clk(Clock), .T(Clock), .Q(t_ff_1_q), .Qn(t_ff_1_qn[0]), .reset(Clear));  // open: preset, en
  T_Flip_Flop t_ff_2 (
    .clk(t_ff_1_q), .T(t_ff_1_q), .Q(t_ff_2_q), .Qn(t_ff_1_qn[1]), .reset(Clear));  // open: preset, en
  not not_1 (not_1_out, Store);
  T_Flip_Flop t_ff_3 (
    .clk(t_ff_2_q), .T(t_ff_2_q), .Q(t_ff_3_q), .Qn(t_ff_1_qn[2]), .reset(Clear));  // open: preset, en
  RAM #(.addrWidth(5), .dataWidth(32), .bus("separate")) ram_2 (
    .addr(out_7), .din(ram_1_data), .data(ram_2_data), .str(not_1_out), .clk(Clock), .clr(Clear));  // open: sel, ld
  T_Flip_Flop t_ff_4 (
    .clk(t_ff_3_q), .T(t_ff_3_q), .Q(t_ff_4_q), .Qn(t_ff_1_qn[3]), .reset(Clear));  // open: preset, en
  T_Flip_Flop t_ff_5 (.clk(t_ff_4_q), .T(t_ff_4_q), .Qn(t_ff_1_qn[4]), .reset(Clear));  // open: Q, preset, en
  Register #(.width(5)) register_1 (.D(t_ff_1_qn), .Q(out_7), .clk(Clock));  // open: en, clr
  Multiplexer #(.width(32)) multiplexer_2 (
    .in0(ram_2_data), .in1({32{1'b0}}), .out(Data_Output), .sel(Clock));  // open: en

  // Other names for the same wires on the sheet: clk = Clock; clr = Clear; str = Store
endmodule

module ControllerAdapter (
  input  [3:0] X_Axis,
  input  [3:0] Y_Axis,
  input  Clock,
  output [15:0] out_4
);

  Register #(.width(16)) register_1 (.D({{8{1'b0}}, Y_Axis, X_Axis}), .Q(out_4), .clk(Clock));  // open: en, clr
endmodule

module MemoryConverter (
  input  [5:0] Address_Input,
  input  [15:0] Data_Input,
  input  Store,
  input  Clock,
  input  Clear,
  output [31:0] Data_Output,
  output [4:0] Address_Output,
  output OutStore
);

  wire and_1_out, and_2_out, not_1_out, or_1_out;

  and and_1 (and_1_out, Store, Address_Input[0]);
  and and_2 (and_2_out, Store, not_1_out);
  not not_1 (not_1_out, Address_Input[0]);
  RAM #(.addrWidth(5), .dataWidth(16), .bus("separate")) ram_1 (
    .addr(Address_Input[5:1]), .din(Data_Input), .data(Data_Output[15:0]), .str(and_1_out), .clk(Clock),
    .clr(Clear));  // open: sel, ld
  RAM #(.addrWidth(5), .dataWidth(16), .bus("separate")) ram_2 (
    .addr(Address_Input[5:1]), .din(Data_Input), .data(Data_Output[31:16]), .str(and_2_out));  // open: sel, clk, ld, clr
  or or_1 (or_1_out, Store, OutStore);
  T_Flip_Flop t_ff_1 (.clk(Clear), .T(or_1_out), .Q(OutStore));  // open: Qn, preset, reset, en

  assign Address_Output = Address_Input[5:1];

  // Other names for the same wires on the sheet: odd = Address_Input[0]; adr[4:0] = Address_Input[5:1]; clk = Clock;
  //   clr = Clear; data[15:0] = Data_Input; str = Store
endmodule
